# Fritzing sketch Stikino4Lilypad (saved by Fritzing 0.9.2b)

parts:
  Componente1 = Lilypad Arduino Board
  Componente2 = SRF05 Ultrasonic Rangefinder
  U1 = LIPO-110mAh [package=lipo-110]
  U2 = Vibration Motor- ROB-08449 [package=vibe-motor-10mm]

nets:
  GND: Componente1.GND, Componente2.GND, U1.-, U2.+
  VCC: Componente1.VCC, Componente2.VCC, U1.+
  N1: Componente1.D6, U2.-
  N2: Componente1.D2, Componente2.Trig

notes:
  Pin n° 2 respond to the PROBE_PIN in the .ino
  Pin n° 6 respond to the VIBE_PIN in the .ino
